# Fritzing sketch Logic_Box_Schematic (saved by Fritzing 1.0.0rc)

parts:
  CR2025 = Battery Holders [package=battcom_20mm_pth]
  CR2025_2 = Battery Holders [package=battcom_20mm_pth]
  R1 = Resistor [tolerance=±5% power=0.25W resistance=330 package=THT]
  LED1 = LED - 5mm [color="Red (633nm)" current=0.030A package="5 mm [THT]"]
  S1 = SWITCH-MOMENTARY-2 [package=tactile_switch_smd-2]
  LED2 = LED - 5mm [color="Blue (505nm)" current=0.030A package="5 mm [THT]"]
  R2 = Resistor [tolerance=±5% power=0.25W resistance=330 package=THT]
  S2 = SWITCH-MOMENTARY-2 [package=tactile_switch_smd-2]
  S3 = SWITCH-MOMENTARY-2 [package=tactile_switch_smd-2]
  R3 = Resistor [tolerance=±5% power=0.25W resistance=330 package=THT]
  LED3 = LED - 5mm [color="Green (560nm)" current=0.030A package="5 mm [THT]"]
  S4 = SWITCH-MOMENTARY-2 [package=tactile_switch_smd-2]
  S5 = SWITCH-MOMENTARY-2 [package=tactile_switch_smd-2]
  R4 = Resistor [tolerance=±5% power=0.25W resistance=10k package=THT]
  R5 = Resistor [tolerance=±5% power=0.25W resistance=10k package=THT]
  74HC86 = 74HC08 Logic AND Gate [part_number=74HC08 package="DIP (Dual Inline) [THT]"]

nets:
  N1: CR2025.+, CR2025_2.-
  N2: CR2025.-, S1.2, S3.2, R4.Pin_1, R5.Pin_1, 74HC86.2A, 74HC86.2B, 74HC86.GND, 74HC86.3A, 74HC86.3B, 74HC86.4A, 74HC86.4B
  N3: CR2025_2.+, R1.Pin_0, R2.Pin_0, R3.Pin_0, 74HC86.VCC
  N4: R1.Pin_1, LED1.anode
  N5: LED1.cathode, S1.1
  N6: LED2.cathode, S2.1
  N7: LED2.anode, R2.Pin_1
  N8: S2.2, S3.1
  N9: R3.Pin_1, LED3.anode
  N10: LED3.cathode, 74HC86.1Y
  N11: S4.2, R5.Pin_0
  N12: S4.1, 74HC86.1A
  N13: S5.2, R4.Pin_0
  N14: S5.1, 74HC86.1B
