# Fritzing sketch PCB_Design (saved by Fritzing 1.0.0rc)
circuit board: 8.47cm x 5.64444cm
breadboards: 1

parts:
  LED2 = JST XH 2A male [form="♂ (male)" package=THT]
  LED3 = JST XH 2A male [form="♂ (male)" package=THT]
  LED1 = male pin header, 2 pins [form="♂ (male)"]
  R1 = Resistor [tolerance=±5% power=0.25W resistance=330 package=THT]
  R2 = Resistor [tolerance=±5% power=0.25W resistance=330 package=THT]
  R3 = Resistor [tolerance=±5% power=0.25W resistance=330 package=THT]
  BTN1 = male pin header, 2 pins [form="♂ (male)"]
  BTN2 = male pin header, 2 pins [form="♂ (male)"]
  BTN3 = male pin header, 2 pins [form="♂ (male)"]
  BTN4 = male pin header, 2 pins [form="♂ (male)"]
  BTN5 = male pin header, 2 pins [form="♂ (male)"]
  PWR = male pin header, 2 pins [form="♂ (male)"]
  R4 = Resistor [tolerance=±5% power=0.25W resistance=330 package=THT]
  R5 = Resistor [tolerance=±5% power=0.25W resistance=330 package=THT]
  IC1 = 74HC08 Logic AND Gate [part_number=74HC08 package="DIP (Dual Inline) [THT]"]

nets:
  N1: LED2.pin1, R2.Pin_1
  N2: LED2.pin2, BTN2.pin1
  N3: LED3.pin1, R3.Pin_0
  N4: LED3.pin2, BTN1.pin2, BTN3.pin2, PWR.pin2, R4.Pin_1, R5.Pin_1, IC1.2A, IC1.2B, IC1.GND, IC1.3A, IC1.3B, IC1.4A, IC1.4B
  N5: LED1.pin1, R1.Pin_1
  N6: LED1.pin2, BTN1.pin1
  N7: R1.Pin_0, R2.Pin_0, BTN4.pin1, BTN5.pin1, PWR.pin1, IC1.VCC
  N8: R3.Pin_1, IC1.1Y
  N9: BTN2.pin2, BTN3.pin1
  N10: BTN4.pin2, R4.Pin_0, IC1.1A
  N11: BTN5.pin2, R5.Pin_0, IC1.1B

notes:
  v 2.1
  +

custom parts:
  JST XH 2A male: JST XH-2A
